// Digital circuit UTS NO 10.dig as structural Verilog
module UTS_NO_10 (
  input  W,
  input  X,
  input  Y,
  input  Z,
  output P
);

  wire and_1_out, and_2_out, and_3_out, and_4_out, and_5_out, not_1_out, not_2_out, not_3_out;

  not not_1 (not_1_out, W);
  not not_2 (not_2_out, X);
  not not_3 (not_3_out, Z);
  and and_1 (and_1_out, W, X, Y, Z);
  and and_2 (and_2_out, W, not_2_out);
  and and_3 (and_3_out, W, X, Y);
  and and_4 (and_4_out, not_1_out, Y, not_3_out);
  and and_5 (and_5_out, W, not_2_out, Y);
  or or_1 (P, and_3_out, and_2_out, and_4_out, and_5_out, and_1_out);

  // Notes on the sheet:
  //   Bayu Syamsi Samudra
  //   wxyz + wx' + wx'y + wxy + w'yz'
endmodule
