// Digital circuit UTS NO 3.dig as structural Verilog
module UTS_NO_3 (
  input  X,
  input  Y,
  input  Z,
  output Q
);

  wire and_1_out, and_2_out, not_3_out;

  // Not not_1 has open pins: in=X, out=open
  // Not not_2 has open pins: in=Y, out=open
  not not_3 (not_3_out, Z);
  and and_1 (and_1_out, X, Y);
  and and_2 (and_2_out, Y, not_3_out);
  or or_1 (Q, and_1_out, and_2_out);

  // Notes on the sheet:
  //   Bayu Syamsi Samudra
  //   x' y 'z + yz' + xy
endmodule
