// Digital circuit UTS NO 8.dig as structural Verilog
module UTS_NO_8 (
  input  A,
  input  B,
  input  C,
  input  D,
  output P
);

  wire and_1_out, and_2_out, and_3_out, and_4_out, and_5_out, not_1_out, not_2_out, not_3_out;

  not not_1 (not_1_out, A);
  not not_2 (not_2_out, C);
  not not_3 (not_3_out, D);
  and and_1 (and_1_out, not_1_out, B, not_3_out);
  and and_2 (and_2_out, B, C, D);
  and and_3 (and_3_out, B, D);
  and and_4 (and_4_out, A, B, C);
  and and_5 (and_5_out, A, B, not_2_out);
  or or_1 (P, and_1_out, and_4_out, and_3_out, and_2_out, and_5_out);

  // Notes on the sheet:
  //   Bayu Syamsi Samudra
  //   A 'BD + BDC + ABC' + BD + ABC
endmodule
